# Fritzing sketch wiring (saved by Fritzing 0.9.5d)
stripboards: 4

parts:
  kEYPAD_MATRICIAL_2 = KEYPAD 4x3
  J28 = male pin header, 4 pins [form="♂ (male)"]
  J30 = male pin header, 2 pins [form="♂ (male)"]
  J36 = male pin header, 2 pins [form="♂ (male)"]
  J37 = male pin header, 2 pins [form="♂ (male)"]
  J39 = male pin header, 2 pins [form="♂ (male)"]
  J40 = male pin header, 2 pins [form="♂ (male)"]
  J41 = male pin header, 2 pins [form="♂ (male)"]
  J45 = male pin header, 2 pins [form="♂ (male)"]
  J47 = male pin header, 7 pins [form="♂ (male)"]
  J48 = Piezo Speaker
  LED3 = smd LED [color="Red (633nm)" package="0603 [SMD]"]
  LED4 = smd LED [color="Yellow (595nm)" package="0603 [SMD]"]
  DFRobot_DFPlayer_Mini2 = DFRobot DFPlayer Mini [part_number=DFR0299]
  R6 = Resistor [tolerance=±5% resistance=100 package="2512 [SMD]"]
  R7 = Resistor [tolerance=±5% resistance=220 package="2512 [SMD]"]
  R8 = Resistor [tolerance=±5% resistance=220 package="2512 [SMD]"]
  Part5 = LCD1602-I2C
  SPKR2 = Loudspeaker
  U4 = SWITCH_SPDT [package=kps-1290]
  U5 = SWITCH_SPDT [package=kps-1290]
  VCC2 = Battery block 9V
  Part6 = Arduino Nano (Rev3.0)  # not connected
  J49 = female pin header, 7 pins [form="♀ (female)"]
  J50 = female pin header, 4 pins [form="♀ (female)"]
  J51 = female pin header, 2 pins [form="♀ (female)"]
  J53 = female pin header, 2 pins [form="♀ (female)"]
  J55 = female pin header, 2 pins [form="♀ (female)"]
  J57 = rounded female pin header, 3 pins [form="♀ (female rounded)"]
  J58 = rounded female pin header, 3 pins [form="♀ (female rounded)"]
  J59 = rounded female pin header, 1 pin [form="♀ (female rounded)"]
  J61 = female pin header, 2 pins [form="♀ (female)"]
  J62 = female pin header, 2 pins [form="♀ (female)"]
  J64 = female pin header, 2 pins [form="♀ (female)"]
  R9 = Resistor [tolerance=±5% resistance=10k package="2512 [SMD]"]
  J63 = female pin header, 8 pins [form="♀ (female)"]
  J52 = rounded female pin header, 1 pin [form="♀ (female rounded)"]
  J65 = female pin header, 3 pins [form="♀ (female)"]
  J66 = female pin header, 2 pins [form="♀ (female)"]
  J67 = female pin header, 2 pins [form="♀ (female)"]
  J68 = female pin header, 1 pin [form="♀ (female)"]
  J69 = rounded female pin header, 1 pin [form="♀ (female rounded)"]
  J70 = female pin header, 2 pins [form="♀ (female)"]
  J71 = rounded female pin header, 1 pin [form="♀ (female rounded)"]
  J60 = rounded female pin header, 1 pin [form="♀ (female rounded)"]
  J54 = female pin header, 3 pins [form="♀ (female)"]

nets:
  N1: kEYPAD_MATRICIAL_2.col1, J47.pin1
  N2: kEYPAD_MATRICIAL_2.arrow1, J47.pin2
  N3: kEYPAD_MATRICIAL_2.col2, J47.pin3
  N4: kEYPAD_MATRICIAL_2.arrow2, J47.pin4
  N5: kEYPAD_MATRICIAL_2.col3, J47.pin5
  N6: kEYPAD_MATRICIAL_2.arrow3, J47.pin6
  N7: kEYPAD_MATRICIAL_2.arrow4, J47.pin7
  N8: J28.pin1, DFRobot_DFPlayer_Mini2.VCC
  N9: J28.pin3, DFRobot_DFPlayer_Mini2.TX
  N10: J28.pin4, DFRobot_DFPlayer_Mini2.RX
  N11: J30.pin1, U4.P
  N12: J30.pin2, U4.S
  N13: J36.pin1, Part5.GND
  N14: J36.pin2, Part5.VCC
  N15: J37.pin1, Part5.SCL
  N16: J37.pin2, Part5.SDA
  N17: J39.pin1, LED3.cathode
  N18: J39.pin2, R8.Pin_0
  N19: J40.pin1, LED4.cathode
  N20: J40.pin2, R7.Pin_0
  N21: J41.pin1, J48.pin1
  N22: J41.pin2, R6.Pin_0
  N23: J45.pin1, VCC2.-
  N24: J45.pin2, U5.P
  N25: J48.pin2, R6.Pin_1
  N26: LED3.anode, R8.Pin_1
  N27: LED4.anode, R7.Pin_1
  N28: DFRobot_DFPlayer_Mini2.SPK_1, SPKR2.pin2
  N29: DFRobot_DFPlayer_Mini2.GND-1, SPKR2.pin1
  N30: U5.O, VCC2.+
  N31: J49.pin1, J63.pin1
  N32: J49.pin2, J63.pin2
  N33: J49.pin3, J63.pin3
  N34: J49.pin4, J63.pin4
  N35: J49.pin5, J63.pin5
  N36: J49.pin6, J63.pin6
  N37: J49.pin7, J63.pin7
  N38: J50.pin1, J65.pin1
  N39: J50.pin2, J65.pin2
  N40: J50.pin3, J52.pin1, J65.pin3, J66.pin2
  N41: J50.pin4, J57.pin1, J62.pin1, J68.pin1, J69.pin1, J70.pin2
  N42: J51.pin1, J53.pin2, J55.pin1, J58.pin3, J59.pin1, J61.pin1, J62.pin2, J64.pin1, J64.pin2, R9.Pin_0, J60.pin1
  N43: J51.pin2, J53.pin1
  N44: J55.pin2, J61.pin2
  N45: R9.Pin_1, J70.pin1, J71.pin1, J54.pin1
  N46: J63.pin8, J66.pin1
  N47: J67.pin1, J54.pin2
  N48: J67.pin2, J54.pin3

notes:
  contacts of pin sockets with rounded holes are removed

custom parts:
  KEYPAD 4x3: KEYPAD matricial de 12 botones, 4 filas x 3 columnas
  LCD1602-I2C: A standard character display, usually with 2x16 characters. Comes in many colors with LCM1602 IIC attached.
